# Fritzing sketch Untitled Sketch 2 (saved by Fritzing 0.9.3b)
circuit board: 10cm x 5.4cm
breadboards: 1

parts:
  Composant1 = Arduino Mega 2560 (Rev3)
  J1 = AVR ISP 6 Pin [package=2x3]
  3 = female pin header, 4 pins [form="♀ (female)"]
  5 = female pin header, 4 pins [form="♀ (female)"]
  4 = female pin header, 4 pins [form="♀ (female)"]
  2 = female pin header, 4 pins [form="♀ (female)"]
  J2 = female pin header, 7 pins [form="♀ (female)"]
  J3 = female pin header, 7 pins [form="♀ (female)"]
  J4 = female pin header, 7 pins [form="♀ (female)"]
  J5 = female pin header, 7 pins [form="♀ (female)"]
  J6 = female pin header, 7 pins [form="♀ (female)"]
  J7 = female pin header, 7 pins [form="♀ (female)"]
  6 = female pin header, 4 pins [form="♀ (female)"]
  1 = female pin header, 4 pins [form="♀ (female)"]

nets:
  N1: Composant1.D21/SCL, 3.pin4, 5.pin4, 4.pin4, 2.pin4, 6.pin4, 1.pin4
  N2: Composant1.D20/SDA, Composant1.SDA, 3.pin3, 5.pin3, 4.pin3, 2.pin3, 6.pin3, 1.pin3
  N3: Composant1.GND, 3.pin1, 5.pin1, 4.pin1, 2.pin1, 6.pin1, 1.pin1
  N4: Composant1.3V3, J2.pin7, J3.pin7, J4.pin7, J5.pin7, J6.pin7, J7.pin7
  N5: Composant1.5V, 3.pin2, 5.pin2, 4.pin2, 2.pin2, 6.pin2, 1.pin2
  N6: Composant1.D32, J2.pin1
  N7: Composant1.D36, J3.pin1
  N8: Composant1.D40, J4.pin1
  N9: Composant1.D44, J5.pin1
  N10: Composant1.D48, J6.pin1
  N11: Composant1.D52, J7.pin1
  N12: J1.1, J2.pin4, J3.pin4, J4.pin4, J5.pin4, J6.pin4, J7.pin4
  N13: J1.3, J2.pin2, J3.pin2, J4.pin2, J5.pin2, J6.pin2, J7.pin2
  N14: J1.4, J2.pin3, J3.pin3, J4.pin3, J5.pin3, J6.pin3, J7.pin3
  N15: J1.5, J2.pin6, J3.pin6, J4.pin6, J5.pin6, J6.pin6, J7.pin6
  N16: J1.6, J2.pin5, J3.pin5, J4.pin5, J5.pin5, J6.pin5, J7.pin5

notes:
  I2C
  SPI
