# Fritzing sketch noTouchClock (saved by Fritzing 0.9.3b)
circuit board: 10cm x 5.4cm
breadboards: 1

parts:
  Composant1 = Arduino Mega 2560 (Rev3)
  J1 = AVR ISP 6 Pin [package=2x3]
  3 = female pin header, 4 pins [form="♀ (female)"]
  5 = female pin header, 4 pins [form="♀ (female)"]
  4 = female pin header, 4 pins [form="♀ (female)"]
  2 = female pin header, 4 pins [form="♀ (female)"]
  J2 = female pin header, 7 pins [form="♀ (female)"]
  J3 = female pin header, 7 pins [form="♀ (female)"]
  J4 = female pin header, 7 pins [form="♀ (female)"]
  J5 = female pin header, 7 pins [form="♀ (female)"]
  J6 = female pin header, 7 pins [form="♀ (female)"]
  J7 = female pin header, 7 pins [form="♀ (female)"]
  6 = female pin header, 4 pins [form="♀ (female)"]
  1 = female pin header, 4 pins [form="♀ (female)"]
  J8 = female pin header, 3 pins [form="♀ (female)"]
  J9 = female pin header, 3 pins [form="♀ (female)"]
  J10 = female pin header, 3 pins [form="♀ (female)"]
  J11 = female pin header, 3 pins [form="♀ (female)"]
  J12 = female pin header, 3 pins [form="♀ (female)"]
  J13 = female pin header, 3 pins [form="♀ (female)"]
  J14 = female pin header, 3 pins [form="♀ (female)"]
  J15 = female pin header, 3 pins [form="♀ (female)"]
  J16 = female pin header, 3 pins [form="♀ (female)"]
  J17 = female pin header, 3 pins [form="♀ (female)"]
  J18 = female pin header, 3 pins [form="♀ (female)"]
  J19 = female pin header, 3 pins [form="♀ (female)"]
  J20 = female pin header, 3 pins [form="♀ (female)"]
  J21 = female pin header, 3 pins [form="♀ (female)"]

nets:
  N1: Composant1.A0, J14.pin3
  N2: Composant1.A1, J15.pin3
  N3: Composant1.A2, J16.pin3
  N4: Composant1.A3, J17.pin3
  N5: Composant1.A4, J18.pin3
  N6: Composant1.A5, J19.pin3
  N7: Composant1.A6, J20.pin3
  N8: Composant1.A7, J21.pin3
  N9: Composant1.D21/SCL, 3.pin4, 5.pin4, 4.pin4, 2.pin4, 6.pin4, 1.pin4
  N10: Composant1.D20/SDA, 3.pin3, 5.pin3, 4.pin3, 2.pin3, 6.pin3, 1.pin3
  N11: Composant1.3V3, J2.pin7, J3.pin7, J4.pin7, J5.pin7, J6.pin7, J7.pin7
  N12: Composant1.5V, 3.pin2, 5.pin2, 4.pin2, 2.pin2, 6.pin2, 1.pin2, J8.pin2, J9.pin2, J10.pin2, J11.pin2, J12.pin2, J13.pin2, J14.pin2, J15.pin2, J16.pin2, J17.pin2, J18.pin2, J19.pin2, J20.pin2, J21.pin2
  N13: Composant1.GND, 3.pin1, 5.pin1, 4.pin1, 2.pin1, J2.pin5, J3.pin5, J4.pin5, J5.pin5, J6.pin5, J7.pin5, 6.pin1, 1.pin1, J8.pin3, J9.pin3, J10.pin3, J11.pin3, J12.pin3, J13.pin3, J14.pin1, J15.pin1, J16.pin1, J17.pin1, J18.pin1, J19.pin1, J20.pin1, J21.pin1
  N14: Composant1.D2_PWM, J8.pin1
  N15: Composant1.D3_PWM, J13.pin1
  N16: Composant1.D4_PWM, J12.pin1
  N17: Composant1.D5_PWM, J11.pin1
  N18: Composant1.D6_PWM, J9.pin1
  N19: Composant1.D7_PWM, J10.pin1
  N20: Composant1.D30, J2.pin1
  N21: Composant1.D34, J3.pin1
  N22: Composant1.D38, J4.pin1
  N23: Composant1.D42, J5.pin1
  N24: Composant1.D46, J6.pin1
  N25: Composant1.D50, J7.pin1
  N26: J1.1, J2.pin4, J3.pin4, J4.pin4, J5.pin4, J6.pin4, J7.pin4
  N27: J1.3, J2.pin2, J3.pin2, J4.pin2, J5.pin2, J6.pin2, J7.pin2
  N28: J1.4, J2.pin3, J3.pin3, J4.pin3, J5.pin3, J6.pin3, J7.pin3
  N29: J1.5, J2.pin6, J3.pin6, J4.pin6, J5.pin6, J6.pin6, J7.pin6

notes:
  I2C
  SPI
